// Logisim project Circuito.circ as structural Verilog: 1 circuit, main circuit main
module main (
  input  A,
  input  B,
  input  C,
  input  A2,
  input  B2,
  input  C2,
  output _21
);

  wire and_1_out, and_2_out, or_1_out, or_2_out, xnor_1_out, xnor_2_out, xnor_3_out, xor_1_out;

  or or_1 (or_1_out, A, C);
  xor xor_1 (xor_1_out, B, C);
  and and_1 (and_1_out, A, C);
  and and_2 (and_2_out, or_1_out, B);
  or or_2 (or_2_out, and_1_out, ~B);  // OR_Gate
  xnor xnor_1 (xnor_1_out, and_2_out, A2);
  xnor xnor_2 (xnor_2_out, xor_1_out, B2);
  xnor xnor_3 (xnor_3_out, C2, or_2_out);
  and and_3 (_21, xnor_1_out, xnor_2_out, xnor_3_out);

  // Notes on the sheet:
  //   1
  //   2
  //   3
  //   4
  //   5
  //   6
  //   7
  //   8
  //   9
  //   10
  //   11
  //   12
  //   13
  //   17
  //   14
  //   15
  //   16
  //   18
  //   19
  //   20
endmodule
